# Fritzing sketch Schematic_V00 (saved by Fritzing 0.9.3b)

parts:
  U1 = ESP32S-HiLetgo [part_number=ESP32S-HiLetgo]
  Componente2 = RFID-RC522-v3

nets:
  N1: U1.GPIO27, Componente2.RST
  N2: U1.GPIO13, Componente2.GND
  VIN: U1.VIN, Componente2.3.3V
  N3: U1.GPIO5, Componente2.SDA
  N4: U1.GPIO18, Componente2.SCK
  N5: U1.GPIO19, Componente2.MISO
  N6: U1.GPIO23, Componente2.MOSI

custom parts:
  ESP32S-HiLetgo: HiLetgo ESP-WROOM-32 ESP32 ESP-32S Development Board 2.4GHz Dual-Mode WiFi + Bluetooth Dual Cores Microcontroller The ESP32 integrated with Antenna switches, RF Balun, power amplifiers, low-noise amplifiers, filters, and management modules, and the entire solution occupies the least area of PCB. 2.4 GHz Wi-Fi plus Bluetooth dual-mode chip, with TSMC Ultra-low power consumption 40nm technology,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
  RFID-RC522-v3: A simple China made RFID-RC522 Reader (6x4 cm); do check the pin labels, as this is a MFRC522 based clone.
